# Fritzing sketch plb (saved by Fritzing 0.9.3b)
breadboards: 1

parts:
  Part1 = Arduino Uno (Rev3) - ICSP
  LED1 = smd LED [color="Red (633nm)" package="1206 [SMD]"]
  LED2 = smd LED [color="Red (633nm)" package="1206 [SMD]"]
  LED3 = smd LED [color="Red (633nm)" package="1206 [SMD]"]
  LED4 = smd LED [color="Red (633nm)" package="1206 [SMD]"]
  S1 = Pushbutton [package="[THT]"]
  R1 = Resistor [tolerance=±5% resistance=220 package=THT]

nets:
  N1: Part1.A2, S1.Pin_3, S1.Pin_4, R1.Pin_1
  N2: Part1.D1/TX, LED1.anode
  N3: Part1.D3_PWM, LED2.anode
  N4: Part1.D5_PWM, LED3.anode
  N5: Part1.D7, LED4.anode
  N6: Part1.GND, LED1.cathode, LED2.cathode, LED3.cathode, LED4.cathode, R1.Pin_0
  N7: S1.Pin_1, S1.Pin_2
